# Fritzing sketch SchaltplanFenster (saved by Fritzing 1.0.5)
breadboards: 1

parts:
  esp1 = ESP32 DevKitc V4
  R1 = Resistor [tolerance=±5% resistance=10k package="0402 [SMD]"]
  WeMos_D1_Mini_DC_Power_Shield1 = WeMos D1 Mini DC Power Shield
  DHT1 = DHT22 Humidity and Temperature Sensor
  Mod1 = KY-021 Mini Magnetic Reed Switch Module [package="Breakout board"]
  R2 = Resistor [tolerance=±5% resistance=10k package="1206 [SMD]"]
  S1 = Round Pushbutton
  R3 = Resistor [tolerance=±5% resistance=10k package="0402 [SMD]"]
  Driver1 = 28BYJ-48 Driver Module [part_number=ULN2003 package=THT]
  SM1 = 28BYJ-48 Stepper Motor [part_number=28BYJ-48]
  SM3 = 28BYJ-48 Stepper Motor [part_number=28BYJ-48]
  Driver3 = 28BYJ-48 Driver Module [part_number=ULN2003 package=THT]
  TD-er1 = MH-Z19 CO2 sensor [part_number=MH-Z19]

nets:
  N1: esp1.IO16, Driver3.IN4
  N2: esp1.IO17, Driver3.IN3
  N3: esp1.IO5, Driver3.IN2
  N4: esp1.IO18, Driver3.IN1
  N5: esp1.IO19, Mod1.S, R2.Pin_0
  N6: esp1.IO21, R1.Pin_1, DHT1.DATA
  N7: esp1.RX, TD-er1.TX
  N8: esp1.TX, TD-er1.RX
  N9: esp1.IO23, S1.leg0, R3.Pin_1
  N10: esp1.GND#18, R3.Pin_0, TD-er1.GND
  N11: esp1.3V3, S1.leg1
  N12: esp1.IO32, Driver1.IN1
  N13: esp1.IO33, Driver1.IN2
  N14: esp1.IO25, Driver1.IN3
  N15: esp1.IO26, Driver1.IN4
  GND: esp1.GND#32, WeMos_D1_Mini_DC_Power_Shield1.G, DHT1.GND, Mod1.-, R2.Pin_1, Driver1.GND, Driver3.GND
  5V: esp1.5V, WeMos_D1_Mini_DC_Power_Shield1.5V, TD-er1.Vin
  3V3: R1.Pin_0, WeMos_D1_Mini_DC_Power_Shield1.3V3, DHT1.VDD, Mod1.Vin
  N16: Driver1.blue-pin, SM1.blue-pin
  N17: Driver1.pink-pin, SM1.pink-pin
  N18: Driver1.yellow-pin, SM1.yellow-pin
  N19: Driver1.orange-pin, SM1.orange-pin
  N20: Driver1.red-pin, SM1.red-pin
  N21: SM3.blue-pin, Driver3.blue-pin
  N22: SM3.pink-pin, Driver3.pink-pin
  N23: SM3.yellow-pin, Driver3.yellow-pin
  N24: SM3.orange-pin, Driver3.orange-pin
  N25: SM3.red-pin, Driver3.red-pin

custom parts:
  ESP32 DevKitc V4: ESP32-DevKitC board with ESP32-WROOM-32 module. ESP32-DevKitC V4 is a small-sized ESP32-based development board produced by Espressif. Most of the pins on the ESP module are broken out to the pin headers on the board. The pins D0, D1, D2, D3, CMD and CLK are used internally for communication between ESP32 and SPI flash memory. They are grouped on both sides near the USB connector. Avoid using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
  WeMos D1 Mini DC Power Shield: A DC shield to allow for 7-24V power supplies.
  KY-021 Mini Magnetic Reed Switch Module: KY-021 magnetic reed switch module. A reed switch is a magnetic sensor that is normally open and gets closed when exposed to a magnetic field.
  28BYJ-48 Driver Module: High-power ULN2003 Stepper Motor Driver Board Test Module For Arduino AVR SMD
  28BYJ-48 Stepper Motor: Unipolar Stepper Motor 28BYJ-48 Top coil - pink & orange Bottom coil - blue & yellow Common rail - red Connector pins: blue - pink - yellow - orange - red
